# Fritzing sketch Prototype0 (saved by Fritzing 0.9.4)
breadboards: 1

parts:
  Part1 = Arduino Uno (Rev3)
  Part2 = BH1750
  OLED1 = OLED 128x64 I2C Monochrome Display

nets:
  N1: Part1.A4/SDA, Part2.SDA, OLED1.SDA
  N2: Part1.A5/SCL, Part2.SCL, OLED1.SCK
  5V: Part1.5V, Part2.VCC, OLED1.VDD
  GND: Part1.GND, Part2.GND, OLED1.GND

custom parts:
  BH1750: Light Sensor
