# Fritzing sketch Prototype1 (saved by Fritzing 0.9.4)
breadboards: 1

parts:
  Part1 = Arduino Uno (Rev3)
  Part2 = BH1750  # not connected
  OLED1 = OLED 128x64 I2C Monochrome Display
  S1 = Pushbutton [package="[THT]"]
  POT1 = Breadboard Trimpot
  POT2 = Breadboard Trimpot

nets:
  N1: Part1.A0, POT1.PIN2
  N2: Part1.A1, POT2.PIN2
  N3: Part1.A4/SDA, OLED1.SDA
  N4: Part1.A5/SCL, OLED1.SCK
  N5: Part1.D2, S1.Pin_3, S1.Pin_4
  5V: Part1.5V, OLED1.VDD, POT1.PIN1, POT2.PIN1
  GND: Part1.GND, OLED1.GND, S1.Pin_1, S1.Pin_2, POT1.PIN3, POT2.PIN3

custom parts:
  BH1750: Light Sensor
