# Fritzing sketch Prototype3 (saved by Fritzing 0.9.4)

parts:
  Part1 = Adafruit Feather M0 Express [part_number="Adafruit #3403"]  # not connected
  Part3 = Adafruit BH1750 [part_number="Adafruit #4681"]
  Part4 = Adafruit I2C QT Rotary Encoder [part_number="Adafruit #4991"]
  Part5 = Adafruit I2C QT Rotary Encoder [part_number="Adafruit #4991"]
  Part6 = Adafruit 128x64 OLED FeatherWing [part_number="Adafruit #4650"]

nets:
  GND: Part3.GND, Part4.GND, Part5.GND, Part6.GND
  VCC: Part3.VCC, Part4.VCC, Part5.VCC, Part6.3.3V
  N1: Part3.SDA, Part4.SDA, Part5.SDA, Part6.SDA
  N2: Part3.SCL, Part4.SCL, Part5.SCL, Part6.SCL

custom parts:
  Adafruit Feather M0 Express: We love all our Feathers equally, but this Feather is very special. It's our first Feather that is specifically designed for use with CircuitPython! CircuitPython is our beginner-oriented flavor of MicroPython - and as the name hints at, its a small but full-featured version of the popular Python programming language specifically for use with circuitry and electronics. That doesn't mean you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
  Adafruit BH1750: This is the BH1750 16-bit Ambient Light sensor from Rohm. Because of how important it is to humans and most other living things, sensing the amount of light in an environment is a common place to get started when learning to work with microcontrollers and sensors. Should we turn up the brightness of our display or dim it to save power? Which direction should your robot move to stay in an area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
  Adafruit I2C QT Rotary Encoder: Rotary encoders are soooo much fun! Twist em this way, then twist them that way. Unlike potentiometers, they go all the way around, and often have little detents for tactile feedback. But, if you've ever tried to add encoders to your project you know that they're a real challenge to use: timers, interrupts, debouncing... This Stemma QT breakout makes all that frustration go away - solder in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
  Adafruit 128x64 OLED FeatherWing: A Feather board without ambition is a Feather board without FeatherWings! This is the FeatherWing 128x64 OLED: it adds a gorgeous 128x64 monochrome OLED plus 3 user buttons to any Feather main board. Using our Feather Stacking Headers or Feather Female Headers you can connect a FeatherWing on top of your Feather board and let the board take flight! These displays are small, only about 1.3"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
